# Fritzing sketch spookyWiring (saved by Fritzing 0.9.3b)
breadboards: 1

parts:
  <–ATTiny85_Dimple_on_top! = attiny85 [package=dip]
  coin_cell_battery_(CR2032) = LilyPad Coin Cell Battery Holder
  piezo_speaker = Piezo Speaker
  LED3 = LED - 3mm [color="Infrared (940nm)" package="3 mm [THT]"]
  LED4 = LED - 3mm [color="White (4500K)" package="3 mm [THT]"]
  <–top_resistor_22kΩ_(red_red_orange_gold) = Resistor [tolerance=±5% resistance=22k package="2512 [SMD]"]
  <–bottom_resistor_220Ω_(red_red_brown_gold) = Resistor [tolerance=±5% resistance=220 package="2512 [SMD]"]

nets:
  N1: <–ATTiny85_Dimple_on_top!.Pin_2, piezo_speaker.pin2
  N2: <–ATTiny85_Dimple_on_top!.Pin_3, piezo_speaker.pin1
  N3: <–ATTiny85_Dimple_on_top!.Pin_4, coin_cell_battery_(CR2032).-, LED4.cathode, <–top_resistor_22kΩ_(red_red_orange_gold).Pin_0
  N4: <–ATTiny85_Dimple_on_top!.Pin_7, LED3.anode, <–top_resistor_22kΩ_(red_red_orange_gold).Pin_1
  N5: <–ATTiny85_Dimple_on_top!.Pin_8, coin_cell_battery_(CR2032).+, LED3.cathode, <–bottom_resistor_220Ω_(red_red_brown_gold).Pin_0
  N6: LED4.anode, <–bottom_resistor_220Ω_(red_red_brown_gold).Pin_1

notes:
  <–infrared proximity sensor:
  black LED on top,
  clear LED on bottom
